# Fritzing sketch B3_BlinkBumpLightIRSonicServos2021 (saved by Fritzing 0.9.6b)
breadboards: 1

parts:
  S1 = SPST Switch [package=switch-spdt_kit]
  R2 = Resistor [tolerance=±1% resistance=220 power=0.25 package=THT]
  LED2 = LED - 5mm [color="Red (633nm)" current=0.030 package="5 mm [THT]"]
  R11 = PHOTOCELL [package=photocell-kit]
  R10 = PHOTOCELL [package=photocell-kit]
  R1 = Resistor [tolerance=±1% resistance=220 power=0.25 package=THT]
  Part1 = Arduino Mega 2560 (Rev3)
  LED3 = LED - 5mm [color="Green (565nm)" current=0.030 package="5 mm [THT]"]
  S2 = SPST Switch [package=switch-spdt_kit]
  LED4 = LED - 5mm [color="Blue (470nm)" current=0.030 package="5 mm [THT]"]
  Part4 = Adafruit Motor/Stepper/Servo Shield [part_number="Adafruit #1438"]
  R16 = Resistor [tolerance=±1% power=0.25 resistance=220 package=THT]
  R18 = Resistor [tolerance=±5% power=0.25 resistance=1k package=THT]
  R19 = Resistor [tolerance=±5% power=0.25 resistance=1k package=THT]
  R15 = Resistor [tolerance=±1% power=0.25 resistance=220 package=THT]
  R14 = Resistor [tolerance=±1% power=0.25 resistance=10k package=THT]
  R13 = Resistor [tolerance=±1% power=0.25 resistance=10k package=THT]
  R12 = Resistor [tolerance=±1% power=0.25 resistance=220 package=THT]
  S2_2 = Basic Servo [part_number="Tilt Servo"]
  S1_2 = Basic Servo [part_number="Pan Servo"]
  TCRT5000L2 = TCRT5000L [package="DIP (Dual Inline) [THT]"]
  TCRT5000L1 = TCRT5000L [package="DIP (Dual Inline) [THT]"]
  Part3 = SRF05 Ultrasonic Rangefinder
  LED5 = RGB LED (com. cathode, rbg) [package="5 mm [THT]"]
  R20 = Resistor [tolerance=±1% power=0.25 resistance=220 package=THT]
  J1 = Piezo Speaker

nets:
  N1: S1.P, Part1.D46, LED3.cathode
  GND: S1.S, Part1.GND, S2.S, R16.Pin_1, R18.Pin_1, R19.Pin_0, R14.Pin_0, R13.Pin_0, TCRT5000L2.pin4, TCRT5000L1.pin4, Part3.GND, R20.Pin_1, J1.pin1
  +5V: R2.Pin_0, R11.P$1, R10.P$2, R1.Pin_0, Part4.+5V, Part3.VCC
  N2: R2.Pin_1, LED3.anode
  N3: LED2.cathode, Part1.D47, S2.P
  N4: LED2.anode, R1.Pin_1
  N5: R11.P$2, Part1.A14, R19.Pin_1
  N6: R10.P$1, Part1.A15, R18.Pin_0
  N7: Part1.A10, R14.Pin_1, TCRT5000L2.pin2
  N8: Part1.A11, R13.Pin_1, TCRT5000L1.pin2
  N9: Part1.D22, LED5.blue_anode
  N10: Part1.D23, LED5.red_anode
  N11: Part1.D24, LED5.green_anode
  N12: Part1.D31, J1.pin2
  N13: Part1.D42, R15.Pin_1, TCRT5000L2.pin1
  N14: Part1.D43, R12.Pin_1, TCRT5000L1.pin1
  N15: Part1.D50, Part3.Echo
  N16: Part1.D51, Part3.Trig
  N17: LED4.cathode, R16.Pin_0
  N18: LED4.anode, Part4.D13
  N19: Part4.D10, S1_2.pulse
  N20: Part4.D9, S2_2.pulse
  N21: R15.Pin_0, TCRT5000L2.pin3
  N22: R12.Pin_0, TCRT5000L1.pin3
  N23: LED5.common_cathode, R20.Pin_0

notes:
  IR light sensor wiring is shown as if
  looking down on the back of the
  sensors, i.e., as they are mounted.

custom parts:
  Adafruit Motor/Stepper/Servo Shield: The original Adafruit Motorshield kit is one of our most beloved kits, which is why we decided to make something even better. We have upgraded the shield kit to make the bestest, easiest way to drive DC and Stepper motors. This shield will make quick work of your next robotics project! We kept the ability to drive up to 4 DC motors or 2 stepper motors, but added many improvements: Instead of a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
  TCRT5000L: Infrared relfected light sensor.
