# Fritzing sketch B3_BlinkBumpLightIRSonicServos2024 (saved by Fritzing 0.9.10b)
breadboards: 1

parts:
  S1 = SPST Switch [package=switch-spdt_kit]
  R2 = Resistor [tolerance=±1% resistance=220 power=0.25 package=THT]
  LED2 = LED - 5mm [color="Red (633nm)" current=0.030 package="5 mm [THT]"]
  R11 = PHOTOCELL [package=photocell-kit]
  R10 = PHOTOCELL [package=photocell-kit]
  R1 = Resistor [tolerance=±1% resistance=220 power=0.25 package=THT]
  Part1 = Arduino Mega 2560 (Rev3)
  LED3 = LED - 5mm [color="Green (565nm)" current=0.030 package="5 mm [THT]"]
  S2 = SPST Switch [package=switch-spdt_kit]
  LED4 = LED - 5mm [color="Blue (470nm)" current=0.030 package="5 mm [THT]"]
  Part4 = Adafruit Motor/Stepper/Servo Shield [part_number="Adafruit #1438"]
  R16 = Resistor [tolerance=±1% power=0.25 resistance=220 package=THT]
  R18 = Resistor [tolerance=±5% power=0.25 resistance=10k package=THT]
  R19 = Resistor [tolerance=±5% power=0.25 resistance=10k package=THT]
  R15 = Resistor [tolerance=±1% power=0.25 resistance=220 package=THT]
  R14 = Resistor [tolerance=±1% power=0.25 resistance=10k package=THT]
  R13 = Resistor [tolerance=±1% power=0.25 resistance=10k package=THT]
  R12 = Resistor [tolerance=±1% power=0.25 resistance=220 package=THT]
  TCRT5000L2 = TCRT5000L [package="DIP (Dual Inline) [THT]"]
  TCRT5000L1 = TCRT5000L [package="DIP (Dual Inline) [THT]"]
  Part3 = SRF05 Ultrasonic Rangefinder
  S1_2 = Basic Servo [part_number="Pan Servo"]
  R20 = Resistor [tolerance=±1% power=0.25 resistance=220 package=THT]
  LED5 = RGB LED (com. cathode, rbg) [package="5 mm [THT]"]
  buz1 = Piezo Buzzer

nets:
  N1: S1.P, Part1.D52, LED3.cathode
  GND: S1.S, Part1.GND, S2.S, R16.Pin_1, R18.Pin_1, R19.Pin_0, R14.Pin_0, R13.Pin_0, TCRT5000L2.pin4, TCRT5000L1.pin4, Part3.GND, R20.Pin_1, buz1.pin_2
  VCC: R2.Pin_0, R11.P$1, R10.P$2, R1.Pin_0, Part4.+5V, Part3.VCC, S1_2.vcc
  N2: R2.Pin_1, LED3.anode
  N3: LED2.cathode, Part1.D53, S2.P
  N4: LED2.anode, R1.Pin_1
  N5: R11.P$2, Part1.A14, R19.Pin_1
  N6: R10.P$1, Part1.A15, R18.Pin_0
  N7: Part1.A10, R14.Pin_1, TCRT5000L2.pin2
  N8: Part1.A11, R13.Pin_1, TCRT5000L1.pin2
  N9: Part1.D31, buz1.pin_1
  N10: Part1.D44, LED5.blue_anode
  N11: Part1.D45, LED5.red_anode
  N12: Part1.D46, LED5.green_anode
  N13: Part1.D48, Part3.Echo
  N14: Part1.D49, Part3.Trig
  N15: Part1.D50, R15.Pin_1, TCRT5000L2.pin1
  N16: Part1.D51, R12.Pin_1, TCRT5000L1.pin1
  N17: LED4.cathode, R16.Pin_0
  N18: LED4.anode, Part4.D13
  GND_2: Part4.GND, S1_2.gnd
  N19: Part4.D10, S1_2.pulse
  N20: R15.Pin_0, TCRT5000L2.pin3
  N21: R12.Pin_0, TCRT5000L1.pin3
  N22: R20.Pin_0, LED5.common_cathode

notes:
  IR light sensor wiring is shown as if
  looking down on the back of the
  sensors, i.e., as they are mounted.
  Sonic sensor pins point UP when mounted on robot and looking forward.

custom parts:
  Adafruit Motor/Stepper/Servo Shield: The original Adafruit Motorshield kit is one of our most beloved kits, which is why we decided to make something even better. We have upgraded the shield kit to make the bestest, easiest way to drive DC and Stepper motors. This shield will make quick work of your next robotics project! We kept the ability to drive up to 4 DC motors or 2 stepper motors, but added many improvements: Instead of a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
  TCRT5000L: Infrared relfected light sensor.
  Piezo Buzzer: Part from https://www.nutsvolts.com/magazine/article/november2012_SmileysWorkshop. Breadboard and icon images modified to be 0.3" in spacing and be more similar to the actual physical part.
